// Logisim project projeto3.circ as structural Verilog: 3 circuits, main circuit main
module main (
  input  in_1
);

  wire ADD, and_1_out, clock_1_out, clock_2_out, DOT, DOTA, LI;
  wire [1:0] OPCODE;
  wire [2:0] Sel_A, Sel_B, Sel_D;
  wire [7:0] adder_1_out, PC_q;
  wire [15:0] alu_1_alu_out, IMMED, multiplexer_1_out, reg_bank_1_a, reg_bank_1_a_1, reg_bank_1_b,
       reg_bank_1_b_1, reg_bank_1_d_reg;
  wire [15:11] rom_1_data;

  Clock clock_1 (.out(clock_1_out));
  Adder adder_1 (.a(8'h1), .b(PC_q), .out(adder_1_out));  // open: cin, cout
  Register PC (.D(adder_1_out), .clk(clock_1_out), .Q(PC_q), .clr(in_1));  // open: en
  ROM #(.dataWidth(16)) rom_1 (.addr(PC_q), .data({rom_1_data, Sel_B, Sel_A, Sel_D, OPCODE}));
  Decoder #(.select(2)) decoder_1 (.out0(LI), .out1(ADD), .out2(DOT), .out3(DOTA), .sel(OPCODE), .en(1'b1));
  and and_1 (and_1_out, rom_1_data[11], rom_1_data[12], rom_1_data[13], rom_1_data[14], rom_1_data[15]);
  assign IMMED = {{5{rom_1_data[15]}}, {rom_1_data, Sel_B, Sel_A}};  // Bit_Extender bit_extender_1
  Multiplexer #(.width(16)) multiplexer_1 (.in0(alu_1_alu_out), .in1(IMMED), .out(multiplexer_1_out), .sel(LI));
  Clock clock_2 (.out(clock_2_out));
  Reg_bank reg_bank_1 (
    .D(multiplexer_1_out), .W_E(1'b1), .Sel_D(Sel_D), .CLK(clock_2_out), .RESET_GERAL(and_1_out),
    .SEL_A(Sel_A), .SEL_B(Sel_B), .D_Reg(reg_bank_1_d_reg), .A(reg_bank_1_a), .A_1(reg_bank_1_a_1),
    .B(reg_bank_1_b), .B_1(reg_bank_1_b_1));
  ALU alu_1 (
    .A(reg_bank_1_a), .B(reg_bank_1_b), .A_1(reg_bank_1_a_1), .OPCODE(OPCODE), .B_1(reg_bank_1_b_1),
    .D_Reg(reg_bank_1_d_reg), .ALU_OUT(alu_1_alu_out));

  // Notes on the sheet:
  //   FORMATO:
  //   li - 00, li rd, immed
  //   add 01 - add rd, rs
  //   dot 10 - dot rd, rs1 
  //   dota 11 - dota rd, rs1, rs2
  //   contents of rom_1 (hex, n*v repeats v):
  //   40 64 88 4c 30 b4 58 5c 2d 42 683 f800
  //   O que vem da ALU
endmodule

// 3
module Reg_bank (
  input  [15:0] D,
  input  W_E,
  input  [2:0] Sel_D,
  input  CLK,
  input  RESET_GERAL,
  input  [2:0] SEL_A,
  input  [2:0] SEL_B,
  output [15:0] D_Reg,
  output [15:0] A,
  output [15:0] A_1,
  output [15:0] B,
  output [15:0] B_1
);

  wire decoder_1_out0, decoder_1_out1, decoder_1_out2, decoder_1_out3, decoder_1_out4, decoder_1_out5,
       decoder_1_out6, decoder_1_out7;
  wire [15:0] register_1_q, register_2_q, register_3_q, register_4_q, register_5_q, register_6_q,
       register_7_q, register_8_q;

  Decoder #(.select(3)) decoder_1 (
    .out0(decoder_1_out0), .out1(decoder_1_out1), .out2(decoder_1_out2), .out3(decoder_1_out3),
    .out4(decoder_1_out4), .out5(decoder_1_out5), .out6(decoder_1_out6), .out7(decoder_1_out7), .sel(Sel_D),
    .en(W_E));
  Register #(.width(16)) register_1 (.D(D), .en(decoder_1_out7), .clk(CLK), .Q(register_1_q), .clr(RESET_GERAL));
  Multiplexer #(.select(3), .width(16)) multiplexer_1 (
    .in0(register_8_q), .in1(register_7_q), .in2(register_6_q), .in3(register_5_q), .in4(register_4_q),
    .in5(register_3_q), .in6(register_2_q), .in7(register_1_q), .out(D_Reg), .sel(Sel_D));
  Register #(.width(16)) register_2 (.D(D), .en(decoder_1_out6), .clk(CLK), .Q(register_2_q), .clr(RESET_GERAL));
  Register #(.width(16)) register_3 (.D(D), .en(decoder_1_out5), .clk(CLK), .Q(register_3_q), .clr(RESET_GERAL));
  Multiplexer #(.select(3), .width(16)) multiplexer_2 (
    .in0(register_8_q), .in1(register_7_q), .in2(register_6_q), .in3(register_5_q), .in4(register_4_q),
    .in5(register_3_q), .in6(register_2_q), .in7(register_1_q), .out(A), .sel(SEL_A));
  Register #(.width(16)) register_4 (.D(D), .en(decoder_1_out4), .clk(CLK), .Q(register_4_q), .clr(RESET_GERAL));
  Multiplexer #(.select(3), .width(16)) multiplexer_3 (
    .in0(register_7_q), .in1(register_6_q), .in2(register_5_q), .in3(register_4_q), .in4(register_3_q),
    .in5(register_2_q), .in6(register_1_q), .in7(register_8_q), .out(A_1), .sel(SEL_A));
  Register #(.width(16)) register_5 (.D(D), .en(decoder_1_out3), .clk(CLK), .Q(register_5_q), .clr(RESET_GERAL));
  Multiplexer #(.select(3), .width(16)) multiplexer_4 (
    .in0(register_8_q), .in1(register_7_q), .in2(register_6_q), .in3(register_5_q), .in4(register_4_q),
    .in5(register_3_q), .in6(register_2_q), .in7(register_1_q), .out(B), .sel(SEL_B));
  Register #(.width(16)) register_6 (.D(D), .en(decoder_1_out2), .clk(CLK), .Q(register_6_q), .clr(RESET_GERAL));
  Register #(.width(16)) register_7 (.D(D), .en(decoder_1_out1), .clk(CLK), .Q(register_7_q), .clr(RESET_GERAL));
  Multiplexer #(.select(3), .width(16)) multiplexer_5 (
    .in0(register_7_q), .in1(register_6_q), .in2(register_5_q), .in3(register_4_q), .in4(register_3_q),
    .in5(register_2_q), .in6(register_1_q), .in7(register_8_q), .out(B_1), .sel(SEL_B));
  Register #(.width(16)) register_8 (.D(D), .en(decoder_1_out0), .clk(CLK), .Q(register_8_q), .clr(RESET_GERAL));

  // Notes on the sheet:
  //   R7
  //   R6
  //   Banco de Registos
  //   R5
  //   R4
  //   R3
  //   R2
  //   R1
  //   R0
endmodule

module ALU (
  input  [15:0] A,
  input  [15:0] B,
  input  [15:0] A_1,
  input  [1:0] OPCODE,
  input  [15:0] B_1,
  input  [15:0] D_Reg,
  output [15:0] ALU_OUT
);

  wire [15:0] adder_1_out, adder_2_out, adder_3_out, multiplier_1_out, multiplier_2_out;

  Multiplier #(.width(16)) multiplier_1 (.a(A), .b(B), .out(multiplier_1_out));  // open: cin, cout
  Multiplier #(.width(16)) multiplier_2 (.a(A_1), .b(B_1), .out(multiplier_2_out));  // open: cin, cout
  Adder #(.width(16)) adder_1 (.a(A), .b(D_Reg), .out(adder_1_out));  // open: cin, cout
  Adder #(.width(16)) adder_2 (.a(multiplier_1_out), .b(multiplier_2_out), .out(adder_2_out));  // open: cin, cout
  Adder #(.width(16)) adder_3 (.a(adder_2_out), .b(D_Reg), .out(adder_3_out));  // open: cin, cout
  Multiplexer #(.select(2), .width(16)) multiplexer_1 (
    .in1(adder_1_out), .in2(adder_2_out), .in3(adder_3_out), .out(ALU_OUT), .sel(OPCODE));  // open: in0
endmodule
