// Logisim project register_bank.circ as structural Verilog: 2 circuits, main circuit main
module main (
);

  wire R0, R1, R2, R3, R4, R5, R6, R7, RA;
  wire [2:0] SelB;

  Multiplexer #(.select(3)) multiplexer_1 (
    .in0(R0), .in1(R1), .in2(R2), .in3(R3), .in4(R4), .in5(R5), .in6(R6), .in7(R7), .out(RA), .sel(SelB));
endmodule

module mux (
);

  wire R0, R1, R2, R3, R4, R5, R6, R7, RA;
  wire [2:0] SelB;

  Multiplexer #(.select(3)) multiplexer_1 (
    .in0(R0), .in1(R1), .in2(R2), .in3(R3), .in4(R4), .in5(R5), .in6(R6), .in7(R7), .out(RA), .sel(SelB));
endmodule
